// Digital circuit misa.dig as structural Verilog
module misa (
  input  clk
);

  wire ctl__add, ctl__negb, ctl__op__adc, ctl__op__add, ctl__op__and, ctl__op__halt, ctl__op__jal,
       ctl__op__jmp, ctl__op__lw, ctl__op__or, ctl__op__rcc, ctl__op__rsr, ctl__op__sbb, ctl__op__set,
       ctl__op__sub, ctl__op__sw, ctl__op__wsr, ctl__op__xor, ctl__port1__write, jk_ff_2_nq, stage__execute,
       stage__fetch, stage__fetchhi, stage__fetchlo;
  wire [1:0] stage;
  wire [3:0] decoder_1_dec__op, decoder_1_dec__rd, decoder_1_dec__rs1, decoder_1_dec__rs2;
  wire [7:0] demultiplexer_1_out_0, demultiplexer_1_out_1, mem__read__data, notconnected_1_out,
       regfile_1_reg__port1__data, regfile_1_reg__port2__data, regfile_1_reg__port3__data;
  wire [15:0] add_1_s, inst, multiplexer_1_out, pc;

  decoder decoder_1 (
    .dec__inst(inst), .dec__op(decoder_1_dec__op), .dec__rd(decoder_1_dec__rd),
    .dec__rs1(decoder_1_dec__rs1), .dec__rs2(decoder_1_dec__rs2));  // open: dec__imm, dec__csr, dec__cmp
  regfile regfile_1 (
    .reg__port1(decoder_1_dec__rd), .reg__port2(decoder_1_dec__rs1), .reg__port3(decoder_1_dec__rs2),
    .reg__port1__write(ctl__port1__write), .reg__port2__write(1'b0), .reg__clk(clk),
    .reg__port1__data(regfile_1_reg__port1__data), .reg__port2__data(regfile_1_reg__port2__data),
    .reg__port3__data(regfile_1_reg__port3__data));
  control control_1 (
    .ctl__stage(stage), .ctl__op(decoder_1_dec__op), .ctl__op__halt(ctl__op__halt),
    .ctl__op__add(ctl__op__add), .ctl__op__adc(ctl__op__adc), .ctl__op__sub(ctl__op__sub),
    .ctl__op__sbb(ctl__op__sbb), .ctl__op__and(ctl__op__and), .ctl__op__or(ctl__op__or),
    .ctl__op__xor(ctl__op__xor), .ctl__op__rrc(ctl__op__rcc), .ctl__op__set(ctl__op__set),
    .ctl__op__lw(ctl__op__lw), .ctl__op__sw(ctl__op__sw), .ctl__op__rsr(ctl__op__rsr),
    .ctl__op__wsr(ctl__op__wsr), .ctl__op__jal(ctl__op__jal), .ctl__op__jmp(ctl__op__jmp));  // open: ctl__port1__write, ctl__port2__write, ctl__negb, ctl__add, ctl__mem__wrback, ctl__mem__rdinst, ctl__mem__read, ctl__mem__write, ctl__use__imm, ctl__use__port1, ctl__use__port2, ctl__use__port3, ctl__wrflags, ctl__branch
  or or_1 (ctl__port1__write, ctl__op__add, ctl__op__adc, ctl__op__sub, ctl__op__sbb, ctl__op__and, ctl__op__or, ctl__op__xor, ctl__op__rcc, ctl__op__set, ctl__op__lw, ctl__op__rsr);
  or or_2 (ctl__negb, ctl__op__sub, ctl__op__sbb);
  or or_3 (ctl__add, ctl__op__add, ctl__op__adc, ctl__op__sub, ctl__op__sbb);
  arithmetic arithmetic_1 (
    .alu__a(regfile_1_reg__port2__data), .alu__b(regfile_1_reg__port3__data), .alu__negb(ctl__negb),
    .alu__and(ctl__op__and), .alu__or(ctl__op__or), .alu__xor(ctl__op__xor), .alu__rot(ctl__op__rcc),
    .alu__cin(ctl__op__sub), .alu__add(ctl__add), .alu__y(regfile_1_reg__port1__data));  // open: alu__z, alu__cout, alu__n, alu__v
  Register #(.Bits(16)) register_1 (.D(add_1_s), .C(clk), .en(1'b1), .Q(pc));
  JK_FF jk_ff_1 (.J(jk_ff_2_nq), .C(clk), .K(1'b1), .Q(stage[0]));  // open: nQ
  Demultiplexer #(.Selector_Bits(2), .Bits(8)) demultiplexer_1 (
    .sel(stage), .in(mem__read__data), .out_0(demultiplexer_1_out_0), .out_1(demultiplexer_1_out_1));  // open: out_2, out_3
  memory memory_1 (
    .mem__write__data(notconnected_1_out), .mem__addr(pc), .mem__read(stage__fetch), .mem__write(1'b0),
    .mem__clk(clk), .mem__read__data(mem__read__data));  // open: mem__ready
  // NotConnected on notconnected_1_out
  Multiplexer #(.Bits(16)) multiplexer_1 (.sel(stage__fetch), .in_0({16{1'b0}}), .in_1(16'h1), .out(multiplexer_1_out));
  JK_FF jk_ff_2 (.J(stage[0]), .C(clk), .K(1'b1), .Q(stage[1]), .nQ(jk_ff_2_nq));
  Register #(.Bits(8)) register_2 (.D(demultiplexer_1_out_0), .C(clk), .en(stage__fetchlo), .Q(inst[7:0]));
  Register #(.Bits(8)) register_3 (.D(demultiplexer_1_out_1), .C(clk), .en(stage__fetchhi), .Q(inst[15:8]));
  Add #(.Bits(16)) add_1 (.a(pc), .b(multiplexer_1_out), .c_i(1'b0), .s(add_1_s));  // open: c_o
  Demultiplexer #(.Selector_Bits(2)) demultiplexer_2 (
    .sel(stage), .in(1'b1), .out_0(stage__fetchlo), .out_1(stage__fetchhi), .out_2(stage__execute));  // open: out_3
  or or_4 (stage__fetch, stage__fetchhi, stage__fetchlo);

  // Notes on the sheet:
  //   clk: Hz: 10
endmodule
